# Fritzing sketch TTGOTelemetryBoard_stripboard (saved by Fritzing 0.9.5d)
stripboards: 1

parts:
  TTGO-T1 = TTGO-T1
  Part1 = Adafruit ADXL345 [part_number="Adafruit #1231"]
  Part2 = MPL3115A2 I2C Barometric Pressure, Altitude, Temperature Sensor
  Part3 = Adafruit DS3231 [part_number="Adafruit #3013"]
  Part4 = Lithium Ion Polymer Battery 3.7v 350mAh [part_number=2750]

nets:
  3.3V: TTGO-T1.3v3, TTGO-T1.SD3, Part1.VIN, Part2.VIN, Part3.Vin
  GND: TTGO-T1.GND, Part1.GND, Part2.GND, Part3.GND
  N1: TTGO-T1.D13, TTGO-T1.D21, Part1.SDA/SDIO, Part2.SDA, Part3.SDA
  N2: TTGO-T1.D22, Part1.SCL, Part2.SCL, Part3.SCL
  N3: Part4.positive, Part4.negative

custom parts:
  TTGO-T1: The TTGO-1 is a complete USB-based microcontoller development system, based on the ESP32 processor, in a very small footprint, capable of implementing many types of projects. All programming is done via the USB port. No special programmer is needed, only a standard micro-USB cable and a PC or Macintosh with a USB port.
  Adafruit ADXL345: Filling out our accelerometer offerings, we now have the really lovely digital ADXL345 from Analog Devices, a triple-axis accelerometer with digital I2C and SPI interface breakout. We added an on-board 3.3V regulator and logic-level shifting circuitry, making it a perfect choice for interfacing with any 3V or 5V microcontroller such as the Arduino. The sensor has three axes of measurements, X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
  MPL3115A2 I2C Barometric Pressure, Altitude, Temperature Sensor: This pressure sensor from Freescale is a great low-cost sensing solution for precision measurement of barometric pressure and altitude. The MPL3115A2 has a typical 1.5 Pascal resolution, which can resolve altitude at 0.3 meters (compare to the BMP180 which can do 0.17m). It has some upsides compared to the BMP180, such as interrupt outputs for ultra-low power usage, and its also a heck of a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
  Adafruit DS3231: The datasheet for the DS3231 explains that this part is an "Extremely Accurate I²C-Integrated RTC/TCXO/Crystal". And, hey, it does exactly what it says on the tin! This Real Time Clock (RTC) is the most precise you can get in a small, low power package. Most RTCs use an external 32kHz timing crystal that is used to keep time with low current draw. And that's all well and good, but those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
  Lithium Ion Polymer Battery 3.7v 350mAh: Lithium ion polymer (also known as 'lipo' or 'lipoly') batteries are thin, light and powerful. The output ranges from 4.2V when completely charged to 3.7V. This battery has a capacity of 350mAh for a total of about 1.3 Wh. The batteries come pre-attached with a genuine 2-pin JST-PH connector as shown and include the necessary protection circuitry.
